// Logisim project registro.circ as structural Verilog: 1 circuit, main circuit main
module main (
  input  \input ,
  input  clear,
  input  in_3,
  input  in_4,
  input  in_5,
  input  in_6,
  input  [1:0] in_7
);

  wire clock_1_out, d_ff_1_q, d_ff_2_q, d_ff_3_q, d_ff_4_q, multiplexer_1_out, multiplexer_2_out,
       multiplexer_3_out, multiplexer_4_out;

  Clock clock_1 (.out(clock_1_out));
  Multiplexer #(.select(2)) multiplexer_1 (
    .in0(\input ), .in1(d_ff_2_q), .in2(in_3), .in3(d_ff_1_q), .out(multiplexer_1_out), .sel(in_7));  // open: en
  D_Flip_Flop d_ff_1 (.clk(clock_1_out), .D(multiplexer_1_out), .Q(d_ff_1_q), .reset(clear));  // open: Qn, preset, en
  D_Flip_Flop d_ff_2 (.clk(clock_1_out), .D(multiplexer_2_out), .Q(d_ff_2_q), .reset(clear));  // open: Qn, preset, en
  Multiplexer #(.select(2)) multiplexer_2 (
    .in0(d_ff_1_q), .in1(d_ff_3_q), .in2(in_4), .in3(d_ff_2_q), .out(multiplexer_2_out), .sel(in_7));  // open: en
  Multiplexer #(.select(2)) multiplexer_3 (
    .in0(d_ff_2_q), .in1(d_ff_4_q), .in2(in_5), .in3(d_ff_3_q), .out(multiplexer_3_out), .sel(in_7));  // open: en
  D_Flip_Flop d_ff_3 (.clk(clock_1_out), .D(multiplexer_3_out), .Q(d_ff_3_q), .reset(clear));  // open: Qn, preset, en
  Multiplexer #(.select(2)) multiplexer_4 (
    .in0(d_ff_3_q), .in2(in_6), .in3(d_ff_4_q), .out(multiplexer_4_out), .sel(in_7));  // open: in1, en
  D_Flip_Flop d_ff_4 (.clk(clock_1_out), .D(multiplexer_4_out), .Q(d_ff_4_q), .reset(clear));  // open: Qn, preset, en

  // Notes on the sheet:
  //   00 derecha
  //   01 Izquierda
  //   10 carga
  //   11 mantenimiento
endmodule
